// Logisim project F3.combine.circ as structural Verilog: 5 circuits, main circuit main
module main (
);

  tfd tfd_1 ();  // open: EN, A1, A0, Y3, Y2, Y1, Y0
endmodule

module tfd (
  input  EN,
  input  A1,
  input  A0,
  output Y3,
  output Y2,
  output Y1,
  output Y0
);

  wire not_1_out, not_2_out;

  not not_1 (not_1_out, A1);
  not not_2 (not_2_out, A0);
  and and_1 (Y3, A1, EN, A0);
  and and_2 (Y2, A1, EN, not_2_out);
  and and_3 (Y1, not_1_out, EN, A0);
  and and_4 (Y0, not_1_out, EN, not_2_out);
endmodule

module ted (
  input  EN,
  input  A2,
  input  A1,
  input  A0,
  output Y7,
  output Y6,
  output Y5,
  output Y4,
  output Y3,
  output Y2,
  output Y1,
  output Y0
);

  wire and_1_out, and_2_out;

  and and_1 (and_1_out, EN, A2);
  and and_2 (and_2_out, EN, ~A2);  // AND_Gate
  tfd tfd_1 (.EN(and_1_out), .A1(A1), .A0(A0), .Y3(Y7), .Y2(Y6), .Y1(Y5), .Y0(Y4));
  tfd tfd_2 (.EN(and_2_out), .A1(A1), .A0(A0), .Y3(Y3), .Y2(Y2), .Y1(Y1), .Y0(Y0));
endmodule

module digtSeven (
  input  [3:0] in_1
);

  wire a, b, c, d, e, f, g, h, n0, n1, n2, n3, n4, n5, n6, n7, n8, n9, n10, n11, n12, n13, n14, n15,
       not_1_out;

  not not_1 (not_1_out, in_1[3]);
  _7_Segment_Display u_7_segment_display_1 (.g(g), .f(f), .a(a), .b(b), .e(e), .d(d), .c(c), .dp(h));
  ted ted_1 (
    .EN(in_1[3]), .A2(in_1[2]), .A1(in_1[1]), .A0(in_1[0]), .Y7(n15), .Y6(n14), .Y5(n13), .Y4(n12), .Y3(n11),
    .Y2(n10), .Y1(n9), .Y0(n8));
  ted ted_2 (
    .EN(not_1_out), .A2(in_1[2]), .A1(in_1[1]), .A0(in_1[0]), .Y7(n7), .Y6(n6), .Y5(n5), .Y4(n4), .Y3(n3),
    .Y2(n2), .Y1(n1), .Y0(n0));
  or or_1 (a, n0, n2, n3, n5, n6, n7, n8, n9, n9);
  or or_2 (b, n0, n1, n2, n3, n4, n7, n8, n9, n9);
  or or_3 (c, n0, n1, n3, n4, n5, n6, n7, n8, n9);
  or or_4 (d, n0, n2, n3, n5, n5, n6, n8, n8, n9);
  or or_5 (e, n0, n2, n6, n8, n8, n8, n8, n8, n8);
  or or_6 (f, n0, n4, n5, n6, n8, n9, n9, n9, n9);
  or or_7 (g, n2, n2, n3, n4, n5, n6, n6, n8, n9);
  nor nor_1 (h, n2, n0, n1, n3, n4, n6, n7, n8, n9, n5);
endmodule

module sevenSegHex (
  input  [3:0] in_1,
  input  hex_enable
);

  wire a, ap, b, bp, c, cp, d, dp, e, ep, f, fp, g, gp, h, hp, n0, n1, n2, n3, n4, n5, n6, n7, n8, n9, n10,
       n11, n12, n13, n14, n15, not_1_out, or_1_out, or_2_out, or_3_out, or_4_out, or_5_out, or_6_out,
       or_7_out;

  not not_1 (not_1_out, in_1[3]);
  or or_1 (or_1_out, gp, n15, n10, n13, n11, n14, n14);
  _7_Segment_Display u_7_segment_display_1 (.g(g), .f(f), .a(a), .b(b), .e(e), .d(d), .c(c), .dp(h));
  or or_2 (or_2_out, ap, ap, n10, n12, n12, n14, n15);
  or or_3 (or_3_out, bp, bp, n13, n13, n13, n10, n10);
  or or_4 (or_4_out, cp, cp, n10, n11, n11, n13, n13);
  or or_5 (or_5_out, dp, dp, n12, n11, n11, n13, n14);
  or or_6 (or_6_out, ep, n15, n12, n10, n11, n13, n14);
  or or_7 (or_7_out, fp, n15, n12, n10, n11, n14, n14);
  and and_1 (h, ~hex_enable, hp);  // AND_Gate
  ted ted_1 (
    .EN(in_1[3]), .A2(in_1[2]), .A1(in_1[1]), .A0(in_1[0]), .Y7(n15), .Y6(n14), .Y5(n13), .Y4(n12), .Y3(n11),
    .Y2(n10), .Y1(n9), .Y0(n8));
  ted ted_2 (
    .EN(not_1_out), .A2(in_1[2]), .A1(in_1[1]), .A0(in_1[0]), .Y7(n7), .Y6(n6), .Y5(n5), .Y4(n4), .Y3(n3),
    .Y2(n2), .Y1(n1), .Y0(n0));
  and and_2 (a, ~h, or_2_out);  // AND_Gate
  and and_3 (b, ~h, or_3_out);  // AND_Gate
  and and_4 (c, ~h, or_4_out);  // AND_Gate
  and and_5 (d, ~h, or_5_out);  // AND_Gate
  and and_6 (e, ~h, or_6_out);  // AND_Gate
  and and_7 (f, ~h, or_7_out);  // AND_Gate
  and and_8 (g, ~h, or_1_out);  // AND_Gate
  or or_8 (ap, n0, n2, n3, n5, n6, n7, n8, n9, n9);
  or or_9 (bp, n0, n1, n2, n3, n4, n7, n8, n9, n9);
  or or_10 (cp, n0, n1, n3, n4, n5, n6, n7, n8, n9);
  or or_11 (dp, n0, n2, n3, n5, n5, n6, n8, n8, n9);
  or or_12 (ep, n0, n2, n6, n8, n8, n8, n8, n8, n8);
  or or_13 (fp, n0, n4, n5, n6, n8, n9, n9, n9, n9);
  or or_14 (gp, n2, n2, n3, n4, n5, n6, n6, n8, n9);
  nor nor_1 (hp, n2, n0, n1, n3, n4, n6, n7, n8, n9, n5);

  // Notes on the sheet:
  //   hex extension
endmodule
